// Logisim project mainboard.circ as structural Verilog: 8 circuits, main circuit main
module main (
  output \уй ,
  output \уй_2 
);

  wire ban, button_1_out, cdm_8_1_p2, cdm_8_1_p4, cdm_8_1_p5, cdm_8_1_p6, cdm_8_1_p8, cdm_8_1_p9, CL, code,
       d0_out, d1_out, d2_out, d3_out, d4_out, d5_out, d6_out, d7_out, d9_out, data, decoder_2_out0,
       decoder_2_out1, demultiplexer_2_out0, demultiplexer_2_out1, hui, I_Osel, in_out, left, mem,
       nand_1_out, nor_1_out, nor_2_out, not_1_out, not_2_out, not_3_out, not_4_out, not_5_out, not_6_out,
       RAM, right, rotl, rotr, st, t_ff_1_q, t_ff_2_q, t_ff_3_q, three, transistor_1_out,
       \вторая_часть_адреса_out , \вужик_вогнепальний , \відсік ;
  wire [3:0] I_Oadr;
  wire [6:0] controlled_buffer_1_out, register_7_q;
  wire [7:0] cdm_8_1_p13, cdm_8_1_p14, controlled_buffer_8_out, controlled_buffer_9_out,
       controlled_buffer_10_out, controlled_buffer_11_out, controlled_buffer_12_out,
       controlled_buffer_13_out, controlled_buffer_14_out, controlled_buffer_15_out,
       controlled_buffer_16_out, demultiplexer_1_out0, demultiplexer_1_out1, I_Odat, pc, register_1_q,
       register_2_q, register_3_q, register_4_q, register_5_q, register_6_q, register_8_q, register_9_q,
       register_10_q, register_11_q, register_12_q, register_13_q, rom_1_data, rom_2_data,
       \пiдрiвнik_1_bus_0_10 , \пiдрiвнik_1_bus_0_11 , \пiдрiвнik_1_bus_0_12 , \пiдрiвнik_1_bus_0_13 ,
       \пiдрiвнik_1_bus_0_14 , \пiдрiвнik_1_bus_0_15 , \пiдрiвнik_1_bus_0_16 , \пiдрiвнik_1_bus_0_17 ;
  wire [7:4] cdm_8_1_p12;
  wire [7:7] rs_latch_1_p3;
  wire [13:0] banner_1_out_2, banner_1_out_3, banner_1_out_4, banner_1_out_5, banner_1_out_6, banner_1_out_7,
       banner_1_out_8, banner_1_out_9;
  wire [31:0] \розширювачі_1_out , \розширювачі_2_out , \розширювачі_3_out , \розширювачі_4_out ,
       \розширювачі_5_out , \розширювачі_6_out , \розширювачі_7_out , \розширювачі_8_out ;

  Register register_1 (.D(controlled_buffer_8_out), .Q(register_1_q), .clk(RAM));  // open: en, clr
  Clock clock_1 (.out(CL));
  // Probe on cdm_8_1_p4
  // Probe on cdm_8_1_p2
  and and_1 (I_Osel, not_1_out, CL, data);
  assign controlled_buffer_1_out = left ? {7{1'b0}} : 7'bz;  // Controlled_Buffer controlled_buffer_1
  Register register_2 (.D(controlled_buffer_9_out), .Q(register_2_q), .clk(RAM));  // open: en, clr
  // Probe on pc
  // Probe on cdm_8_1_p6
  // Probe on cdm_8_1_p5
  Button button_1 (.out(button_1_out));
  not not_1 (not_1_out, nand_1_out);
  and and_2 (RAM, nand_1_out, data);
  Transistor #(.\type ("n")) transistor_1 (.in(1'b0), .out(transistor_1_out), .gate(left));
  Register register_3 (.D(controlled_buffer_10_out), .Q(register_3_q), .clk(RAM));  // open: en, clr
  // Probe on cdm_8_1_p8
  and and_3 (st, data, CL);
  nand nand_1 (nand_1_out, ~cdm_8_1_p12[4], cdm_8_1_p12[5], cdm_8_1_p12[6], cdm_8_1_p12[7]);  // NAND_Gate
  Transistor #(.\type ("n")) transistor_2 (.in(1'b0), .out(transistor_1_out), .gate(right));
  assign controlled_buffer_1_out = right ? 7'b0000001 : 7'bz;  // Controlled_Buffer controlled_buffer_2
  not not_2 (not_2_out, transistor_1_out);
  Register register_4 (.D(controlled_buffer_11_out), .Q(register_4_q), .clk(RAM));  // open: en, clr
  Decoder #(.disabled(0)) decoder_1 (.out0(code), .out1(data), .sel(cdm_8_1_p9), .en(mem));
  // CdM_8 cdm_8_1: pin names not known; wires that end beside it: CL, cdm_8_1_p2, button_1_out, cdm_8_1_p4, cdm_8_1_p5, cdm_8_1_p6, pc, cdm_8_1_p8, cdm_8_1_p9, mem, in_out, {cdm_8_1_p12, I_Oadr}, cdm_8_1_p13, cdm_8_1_p14
  assign cdm_8_1_p14 = in_out ? I_Odat : 8'bz;  // Controlled_Buffer controlled_buffer_3
  Transistor #(.\type ("n")) transistor_3 (.in(1'b0), .out(transistor_1_out), .gate(rotl));
  assign controlled_buffer_1_out = rotl ? 7'b0000010 : 7'bz;  // Controlled_Buffer controlled_buffer_4
  nor nor_1 (nor_1_out, transistor_1_out, not_2_out);
  nor nor_2 (nor_2_out, decoder_2_out1, not_3_out);
  not not_3 (not_3_out, decoder_2_out1);
  Register register_5 (.D(controlled_buffer_12_out), .Q(register_5_q), .clk(RAM));  // open: en, clr
  Demultiplexer #(.width(8), .enable("false")) demultiplexer_1 (
    .out0(demultiplexer_1_out0), .out1(demultiplexer_1_out1), .in({cdm_8_1_p12, I_Oadr}), .sel(\відсік ));
  assign I_Odat = not_4_out ? cdm_8_1_p13 : 8'bz;  // Controlled_Buffer controlled_buffer_5
  not not_4 (not_4_out, in_out);
  Transistor #(.\type ("n")) transistor_4 (.in(1'b0), .out(transistor_1_out), .gate(rotr));
  assign controlled_buffer_1_out = rotr ? 7'b0000011 : 7'bz;  // Controlled_Buffer controlled_buffer_6
  Register register_6 (.D(controlled_buffer_13_out), .Q(register_6_q), .clk(RAM));  // open: en, clr
  // Probe on {cdm_8_1_p12, I_Oadr}
  not not_5 (not_5_out, transistor_1_out);
  Pull_Resistor #(.pull(1)) pull_resistor_1 (.node(transistor_1_out));
  Register #(.width(7), .trigger("high")) register_7 (
    .D(controlled_buffer_1_out), .Q(register_7_q), .clk(not_6_out));  // open: en, clr
  // RS_latch rs_latch_1: pin names not known; wires that end beside it: nor_1_out, nor_2_out, rs_latch_1_p3[7], rs_latch_1_p3[7]
  \пiдрiвнik  \u_пiдрiвнik_1  (
    .bus_0(register_1_q), .bus_0_2(register_2_q), .bus_0_3(register_3_q), .bus_0_4(register_4_q),
    .bus_0_5(register_5_q), .bus_0_6(register_6_q), .bus_0_7(register_8_q), .bus_0_8(register_9_q),
    .bus_0_9(ban), .bus_0_10(\пiдрiвнik_1_bus_0_10 ), .bus_0_11(\пiдрiвнik_1_bus_0_11 ),
    .bus_0_12(\пiдрiвнik_1_bus_0_12 ), .bus_0_13(\пiдрiвнik_1_bus_0_13 ), .bus_0_14(\пiдрiвнik_1_bus_0_14 ),
    .bus_0_15(\пiдрiвнik_1_bus_0_15 ), .bus_0_16(\пiдрiвнik_1_bus_0_16 ), .bus_0_17(\пiдрiвнik_1_bus_0_17 ));
  Register register_8 (.D(controlled_buffer_14_out), .Q(register_8_q), .clk(RAM));  // open: en, clr
  Pull_Resistor pull_resistor_2 (.node(I_Oadr[0]));
  Pull_Resistor pull_resistor_3 (.node(I_Oadr[1]));
  Pull_Resistor pull_resistor_4 (.node(I_Oadr[2]));
  Pull_Resistor pull_resistor_5 (.node(I_Oadr[3]));
  Pull_Resistor pull_resistor_6 (.node(cdm_8_1_p12[4]));
  Pull_Resistor pull_resistor_7 (.node(cdm_8_1_p12[5]));
  Pull_Resistor pull_resistor_8 (.node(cdm_8_1_p12[6]));
  Pull_Resistor pull_resistor_9 (.node(cdm_8_1_p12[7]));
  not not_6 (not_6_out, not_5_out);
  \розширювачі  \u_розширювачі_1  (.in(\пiдрiвнik_1_bus_0_10 ), .Out(\розширювачі_1_out ));
  \розширювачі  \u_розширювачі_2  (.in(\пiдрiвнik_1_bus_0_11 ), .Out(\розширювачі_2_out ));
  \розширювачі  \u_розширювачі_3  (.in(\пiдрiвнik_1_bus_0_12 ), .Out(\розширювачі_3_out ));
  \розширювачі  \u_розширювачі_4  (.in(\пiдрiвнik_1_bus_0_13 ), .Out(\розширювачі_4_out ));
  \розширювачі  \u_розширювачі_5  (.in(\пiдрiвнik_1_bus_0_14 ), .Out(\розширювачі_5_out ));
  \розширювачі  \u_розширювачі_6  (.in(\пiдрiвнik_1_bus_0_15 ), .Out(\розширювачі_6_out ));
  \розширювачі  \u_розширювачі_7  (.in(\пiдрiвнik_1_bus_0_16 ), .Out(\розширювачі_7_out ));
  \розширювачі  \u_розширювачі_8  (.in(\пiдрiвнik_1_bus_0_17 ), .Out(\розширювачі_8_out ));
  Register register_9 (.D(controlled_buffer_15_out), .Q(register_9_q), .clk(RAM));  // open: en, clr
  ROM rom_1 (.addr(demultiplexer_1_out1), .data(rom_1_data), .sel(demultiplexer_2_out1));
  ROM rom_2 (.addr(demultiplexer_1_out0), .data(rom_2_data), .sel(demultiplexer_2_out0));
  RAM ram_1 (.addr({cdm_8_1_p12, I_Oadr}), .data(I_Odat), .sel(RAM), .clk(CL), .ld(in_out));  // open: clr
  assign I_Odat = decoder_2_out1 ? {rs_latch_1_p3[7], register_7_q} : 8'bz;  // Controlled_Buffer controlled_buffer_7
  DotMatrix #(.inputtype("row"), .matrixcols(32), .matrixrows(32)) dotmatrix_1 (
    .row0(\розширювачі_1_out ), .row1(\розширювачі_1_out ), .row2(\розширювачі_1_out ),
    .row3(\розширювачі_1_out ), .row4(\розширювачі_2_out ), .row5(\розширювачі_2_out ),
    .row6(\розширювачі_2_out ), .row7(\розширювачі_2_out ), .row8(\розширювачі_3_out ),
    .row9(\розширювачі_3_out ), .row10(\розширювачі_3_out ), .row11(\розширювачі_3_out ),
    .row12(\розширювачі_4_out ), .row13(\розширювачі_4_out ), .row14(\розширювачі_4_out ),
    .row15(\розширювачі_4_out ), .row16(\розширювачі_5_out ), .row17(\розширювачі_5_out ),
    .row18(\розширювачі_5_out ), .row19(\розширювачі_5_out ), .row20(\розширювачі_6_out ),
    .row21(\розширювачі_6_out ), .row22(\розширювачі_6_out ), .row23(\розширювачі_6_out ),
    .row24(\розширювачі_7_out ), .row25(\розширювачі_7_out ), .row26(\розширювачі_7_out ),
    .row27(\розширювачі_7_out ), .row28(\розширювачі_8_out ), .row29(\розширювачі_8_out ),
    .row30(\розширювачі_8_out ), .row31(\розширювачі_8_out ));
  Button button_2 (.out(left));
  Button button_3 (.out(rotl));
  Multiplexer #(.width(8), .enable("false")) multiplexer_1 (
    .in0(rom_2_data), .in1(rom_1_data), .out(I_Odat), .sel(\відсік ));
  BANNER banner_1 (
    .in_1(ban), .out_2(banner_1_out_2), .out_3(banner_1_out_3), .out_4(banner_1_out_4),
    .out_5(banner_1_out_5), .out_6(banner_1_out_6), .out_7(banner_1_out_7), .out_8(banner_1_out_8),
    .out_9(banner_1_out_9));
  DotMatrix #(.inputtype("row"), .matrixcols(14), .matrixrows(8)) dotmatrix_2 (
    .row0(banner_1_out_2), .row1(banner_1_out_3), .row2(banner_1_out_4), .row3(banner_1_out_5),
    .row4(banner_1_out_6), .row5(banner_1_out_7), .row6(banner_1_out_8), .row7(banner_1_out_9));
  Demultiplexer #(.enable("false")) demultiplexer_2 (
    .out0(demultiplexer_2_out0), .out1(demultiplexer_2_out1), .in(code), .sel(\відсік ));
  Comparator comparator_1 (.a(pc), .b(8'hef), .eq(\вужик_вогнепальний ));  // open: gt, lt
  Hex_Digit_Display hex_digit_display_1 (.value(register_10_q[7:4]));  // open: dp
  Register #(.trigger("low")) register_10 (.D(I_Odat), .Q(register_10_q), .clk(decoder_2_out0));  // open: en, clr
  assign controlled_buffer_8_out = d0_out ? register_12_q : 8'bz;  // Controlled_Buffer controlled_buffer_8
  and d0 (d0_out, register_11_q[7], register_11_q[6], ~register_11_q[5], register_11_q[4], ~register_11_q[3], ~register_11_q[2], ~register_11_q[1], ~register_11_q[0]);  // AND_Gate
  Register register_11 (.D({cdm_8_1_p12, I_Oadr}), .Q(register_11_q), .clk(in_out));  // open: en, clr
  T_Flip_Flop t_ff_1 (.clk(\вужик_вогнепальний ), .T(1'b1), .Q(t_ff_1_q));  // open: Qn, preset, reset, en
  and \u_вторая_часть_адреса  (\вторая_часть_адреса_out , I_Osel, ~I_Oadr[0], ~I_Oadr[1], ~I_Oadr[2], ~I_Oadr[3]);  // AND_Gate
  Hex_Digit_Display hex_digit_display_2 (.value(register_10_q[3:0]));  // open: dp
  Comparator comparator_2 (.a(pc), .b(8'hed), .eq(hui));  // open: gt, lt
  Decoder #(.disabled(0)) decoder_2 (
    .out0(decoder_2_out0), .out1(decoder_2_out1), .sel(in_out), .en(\вторая_часть_адреса_out ));
  LED led_1 (.in(ban));
  Button button_4 (.out(right));
  Button button_5 (.out(rotr));
  assign controlled_buffer_9_out = d1_out ? register_12_q : 8'bz;  // Controlled_Buffer controlled_buffer_9
  and d1 (d1_out, register_11_q[7], register_11_q[6], ~register_11_q[5], register_11_q[4], ~register_11_q[3], ~register_11_q[2], ~register_11_q[1], register_11_q[0]);  // AND_Gate
  Register register_12 (.D(I_Odat), .Q(register_12_q), .clk(in_out));  // open: en, clr
  or or_1 (\відсік , t_ff_1_q, t_ff_3_q, t_ff_2_q);
  T_Flip_Flop t_ff_2 (.clk(hui), .T(1'b1), .Q(t_ff_2_q));  // open: Qn, preset, reset, en
  Comparator comparator_3 (.a(pc), .b(8'heb), .eq(three));  // open: gt, lt
  assign controlled_buffer_10_out = d2_out ? register_12_q : 8'bz;  // Controlled_Buffer controlled_buffer_10
  and d2 (d2_out, register_11_q[7], register_11_q[6], ~register_11_q[5], register_11_q[4], ~register_11_q[3], ~register_11_q[2], register_11_q[1], ~register_11_q[0]);  // AND_Gate
  T_Flip_Flop t_ff_3 (.clk(three), .T(1'b1), .Q(t_ff_3_q));  // open: Qn, preset, reset, en
  assign controlled_buffer_11_out = d3_out ? register_12_q : 8'bz;  // Controlled_Buffer controlled_buffer_11
  and d3 (d3_out, register_11_q[7], register_11_q[6], ~register_11_q[5], register_11_q[4], ~register_11_q[3], ~register_11_q[2], register_11_q[1], register_11_q[0]);  // AND_Gate
  assign controlled_buffer_12_out = d4_out ? register_12_q : 8'bz;  // Controlled_Buffer controlled_buffer_12
  and d4 (d4_out, register_11_q[7], register_11_q[6], ~register_11_q[5], register_11_q[4], ~register_11_q[3], register_11_q[2], ~register_11_q[1], ~register_11_q[0]);  // AND_Gate
  assign controlled_buffer_13_out = d5_out ? register_12_q : 8'bz;  // Controlled_Buffer controlled_buffer_13
  and d5 (d5_out, register_11_q[7], register_11_q[6], ~register_11_q[5], register_11_q[4], ~register_11_q[3], register_11_q[2], ~register_11_q[1], register_11_q[0]);  // AND_Gate
  assign controlled_buffer_14_out = d6_out ? register_12_q : 8'bz;  // Controlled_Buffer controlled_buffer_14
  and d6 (d6_out, register_11_q[7], register_11_q[6], ~register_11_q[5], register_11_q[4], ~register_11_q[3], register_11_q[2], register_11_q[1], ~register_11_q[0]);  // AND_Gate
  assign controlled_buffer_15_out = d7_out ? register_12_q : 8'bz;  // Controlled_Buffer controlled_buffer_15
  and d7 (d7_out, register_11_q[7], register_11_q[6], ~register_11_q[5], register_11_q[4], ~register_11_q[3], register_11_q[2], register_11_q[1], register_11_q[0]);  // AND_Gate
  and d9 (d9_out, register_11_q[0], ~register_11_q[1], ~register_11_q[2], register_11_q[3], register_11_q[4], ~register_11_q[5], register_11_q[6], register_11_q[7]);  // AND_Gate
  ban ban_1 (.in_1(register_13_q), .out_2(ban));
  Register register_13 (.D(controlled_buffer_16_out), .Q(register_13_q), .clk(RAM));  // open: en, clr
  assign controlled_buffer_16_out = d9_out ? register_12_q : 8'bz;  // Controlled_Buffer controlled_buffer_16

  // Other names for the same wires on the sheet: rd_wr = in_out

  // Notes on the sheet:
  //   contents of rom_1 (hex, n*v repeats v):
  //   d0 70 d1 10 a1 d0 71 d1 0 a1 d0 c0 b0 0 e0 15 d0 d9 d1 ff a1 d0 78 b0 d1 1 71 e1 1d 71 ed 20 71 ea
  //   25 d6 80 d0 78 b0 0 e1 2f d0 0 ee 31 88 40 d3 78 ac ee ef 10*0 d0 c0 d1 c8 74 ed 66 c1 b1 8d 45 5 e1
  //   61 1 89 45 d3 c0 77 eb 61 c3 6 8e 4a b7 ab 89 45 c7 ee 53 8c 40 c5 ee 44 ee ed 8*0 d0 70 b0 1 99 54
  //   d2 b0 d3 71 bf 1e a8 8e a8 d7 d0 70 b0 1 95 54 99 99 54 99 54 d2 b0 d3 71 bf 1e a8 d7 d0 70 b0 d2 af
  //   d3 71 bf 1e ac 8f ac 8f ac 8f ac d7 73*0 ee 40 ee
  //   contents of rom_2 (hex, n*v repeats v):
  //   d0 ff d2 d8 a8 d2 c8 a8 ee ef d0 b0 d1 c0 d2 d0 d6 b1 d0 e0 d3 3 d0 e0 f e1 64 c0 d0 a8 d1 b7 d3 8 f
  //   ed 2d b6 a2 88 89 8b 40 ee 22 d6 97 f e0 4d d0 b0 d1 c0 d2 c0 d6 b1 ee ed d0 c0 d1 d0 d6 c6 d0 90 d1
  //   b0 d6 c6 c4 ee 0 ee 61 d0 71 b1 8d 40 a1 d0 a0 d1 c0 d2 d0 d6 b1 d0 a0 d1 b0 d6 c6 d3 3 c4 8b 40 b1
  //   5 e4 18 c0 d2 1 76 ed 72 ee 94 c3 d2 70 bb 5 e1 7c 97 ee 7d 9b ab c7 d2 8 d0 b0 a ed 94 b3 5 e1 8d
  //   2f ee 8e 93 a3 8a 8c 40 ee 83 c4 ee 16 d3 0 d0 a0 d1 c0 d2 9 a ed b0 c0 c1 b0 b5 41 57 c5 c4 8a 8c
  //   8d 40 ee 9f d7 d3 9 f ed c5 c0 c1 b0 b5 51 a9 c4 c5 8c 8d 8e 8b 40 ee b3 d7 d2 9 a ed d3 b3 a7 8c 8d
  //   8a 40 ee c8 d7 25*0 ee 3c ee a
  //   писюн
endmodule

module REGISTERS (
);

  wire [7:0] register_1_q, register_2_q, register_3_q, register_4_q, register_5_q, register_6_q,
       register_7_q, register_8_q;
  wire [31:0] \розширювачі_1_out ;

  Register register_1 (.Q(register_1_q));  // open: D, en, clk, clr
  \розширювачі  \u_розширювачі_1  (.in(register_1_q), .Out(\розширювачі_1_out ));
  \розширювачі  \u_розширювачі_2  (.in(register_2_q));  // open: Out
  Register register_2 (.Q(register_2_q));  // open: D, en, clk, clr
  \розширювачі  \u_розширювачі_3  (.in(register_3_q));  // open: Out
  Register register_3 (.Q(register_3_q));  // open: D, en, clk, clr
  Register register_4 (.Q(register_4_q));  // open: D, en, clk, clr
  \розширювачі  \u_розширювачі_4  (.in(register_5_q));  // open: Out
  Register register_5 (.Q(register_5_q));  // open: D, en, clk, clr
  \розширювачі  \u_розширювачі_5  (.in(register_4_q));  // open: Out
  \розширювачі  \u_розширювачі_6  (.in(register_6_q));  // open: Out
  Register register_6 (.Q(register_6_q));  // open: D, en, clk, clr
  Register register_7 (.Q(register_7_q));  // open: D, en, clk, clr
  \розширювачі  \u_розширювачі_7  (.in(register_7_q));  // open: Out
  \розширювачі  \u_розширювачі_8  (.in(register_8_q));  // open: Out
  Register register_8 (.Q(register_8_q));  // open: D, en, clk, clr
endmodule

module \розширювачі  (
  input  [7:0] in,
  output [31:0] Out
);


  assign Out = {{4{in[7]}}, {4{in[6]}}, {4{in[5]}}, {4{in[4]}}, {4{in[3]}}, {4{in[2]}}, {4{in[1]}}, {4{in[0]}}};
endmodule

module \хитре_інженерне_рішення  (
);

  wire button_1_out, cdm_8_1_p2, cdm_8_1_p4, cdm_8_1_p5, cdm_8_1_p6, cdm_8_1_p7, cdm_8_1_p8, cdm_8_1_p9, CL,
       code, data, mem, not_1_out, rd_wr;
  wire [7:0] cdm_8_1_p12, cdm_8_1_p13, cdm_8_1_p14, cdm_8_1_p15;

  // Probe on cdm_8_1_p4
  // Probe on cdm_8_1_p2
  Clock clock_1 (.out(CL));
  // Probe on cdm_8_1_p5
  // Probe on cdm_8_1_p6
  // Probe on cdm_8_1_p7
  Button button_1 (.out(button_1_out));
  // Probe on cdm_8_1_p8
  // Probe on cdm_8_1_p12
  Decoder #(.disabled(0)) decoder_1 (.out0(code), .out1(data), .sel(cdm_8_1_p9), .en(mem));
  // CdM_8 cdm_8_1: pin names not known; wires that end beside it: CL, cdm_8_1_p2, button_1_out, cdm_8_1_p4, cdm_8_1_p5, cdm_8_1_p6, cdm_8_1_p7, cdm_8_1_p8, cdm_8_1_p9, mem, rd_wr, cdm_8_1_p12, cdm_8_1_p13, cdm_8_1_p14, cdm_8_1_p15
  // Probe on cdm_8_1_p13
  assign cdm_8_1_p14 = rd_wr ? cdm_8_1_p15 : 8'bz;  // Controlled_Buffer controlled_buffer_1
  assign cdm_8_1_p15 = not_1_out ? cdm_8_1_p13 : 8'bz;  // Controlled_Buffer controlled_buffer_2
  not not_1 (not_1_out, rd_wr);
  // Probe on cdm_8_1_p12
  // Probe on cdm_8_1_p15
  ROM rom_1 (.addr(cdm_8_1_p12), .data(cdm_8_1_p15), .sel(code));
  // Probe on cdm_8_1_p15
  RAM ram_1 (.addr(cdm_8_1_p12), .data(cdm_8_1_p15), .sel(data), .clk(CL), .ld(rd_wr));  // open: clr

  // Notes on the sheet:
  //   contents of rom_1 (hex, n*v repeats v):
  //   d2 d2 d1 8 5 e0 16 30 d3 1 f e0 12 8b 8c a8 ee a 8e 89 ee 4 186*0 d1 8 8*0 d4
endmodule

module PC_controller (
  input  [7:0] Sp,
  input  [2:0] decoder,
  input  cl
);

  wire comparator_1_lt;
  wire [2:0] multiplexer_1_out;

  Comparator comparator_1 (.a(Sp), .b(8'h2), .lt(comparator_1_lt));  // open: gt, eq
  Multiplexer #(.width(3), .enable("false")) multiplexer_1 (
    .in0(decoder), .in1(Sp[2:0]), .out(multiplexer_1_out), .sel(comparator_1_lt));
  Register #(.width(3)) register_1 (.D(multiplexer_1_out), .Q(decoder), .clk(cl));  // open: en, clr
endmodule

module \пiдрiвнik  (
  input  [7:0] bus_0,
  input  [7:0] bus_0_2,
  input  [7:0] bus_0_3,
  input  [7:0] bus_0_4,
  input  [7:0] bus_0_5,
  input  [7:0] bus_0_6,
  input  [7:0] bus_0_7,
  input  [7:0] bus_0_8,
  input  bus_0_9,
  output [7:0] bus_0_10,
  output [7:0] bus_0_11,
  output [7:0] bus_0_12,
  output [7:0] bus_0_13,
  output [7:0] bus_0_14,
  output [7:0] bus_0_15,
  output [7:0] bus_0_16,
  output [7:0] bus_0_17
);

  Multiplexer #(.width(8), .enable("false")) multiplexer_1 (
    .in0(bus_0), .in1({8{1'b1}}), .out(bus_0_10), .sel(bus_0_9));
  Multiplexer #(.width(8), .enable("false")) multiplexer_2 (
    .in0(bus_0_2), .in1({8{1'b1}}), .out(bus_0_11), .sel(bus_0_9));
  Multiplexer #(.width(8), .enable("false")) multiplexer_3 (
    .in0(bus_0_3), .in1({8{1'b1}}), .out(bus_0_12), .sel(bus_0_9));
  Multiplexer #(.width(8), .enable("false")) multiplexer_4 (
    .in0(bus_0_4), .in1({8{1'b1}}), .out(bus_0_13), .sel(bus_0_9));
  Multiplexer #(.width(8), .enable("false")) multiplexer_5 (
    .in0(bus_0_5), .in1({8{1'b1}}), .out(bus_0_14), .sel(bus_0_9));
  Multiplexer #(.width(8), .enable("false")) multiplexer_6 (
    .in0(bus_0_6), .in1({8{1'b1}}), .out(bus_0_15), .sel(bus_0_9));
  Multiplexer #(.width(8), .enable("false")) multiplexer_7 (
    .in0(bus_0_7), .in1({8{1'b1}}), .out(bus_0_16), .sel(bus_0_9));
  Multiplexer #(.width(8), .enable("false")) multiplexer_8 (
    .in0(bus_0_8), .in1({8{1'b1}}), .out(bus_0_17), .sel(bus_0_9));
endmodule

module ban (
  input  [7:0] in_1,
  output out_2
);

  or or_1 (out_2, in_1[0], in_1[1], in_1[2], in_1[3], in_1[4], in_1[5], in_1[6], in_1[7]);
endmodule

module BANNER (
  input  in_1,
  output [13:0] out_2,
  output [13:0] out_3,
  output [13:0] out_4,
  output [13:0] out_5,
  output [13:0] out_6,
  output [13:0] out_7,
  output [13:0] out_8,
  output [13:0] out_9
);

  Multiplexer #(.width(14), .enable("false")) multiplexer_1 (.in0({14{1'b0}}), .in1(14'h1892), .out(out_3), .sel(in_1));
  Multiplexer #(.width(14), .enable("false")) multiplexer_2 (.in0({14{1'b0}}), .in1(14'h155a), .out(out_4), .sel(in_1));
  Multiplexer #(.width(14), .enable("false")) multiplexer_3 (.in0({14{1'b0}}), .in1(14'h19d6), .out(out_5), .sel(in_1));
  Multiplexer #(.width(14), .enable("false")) multiplexer_4 (.in0({14{1'b0}}), .in1(14'h1952), .out(out_6), .sel(in_1));
  Multiplexer #(.width(14), .enable("false")) multiplexer_5 (.in0({14{1'b0}}), .in1(14'h1552), .out(out_7), .sel(in_1));
  Multiplexer #(.width(14), .enable("false")) multiplexer_6 (.in0({14{1'b0}}), .in1(14'h1952), .out(out_8), .sel(in_1));

  assign out_2 = {14{1'b0}};
  assign out_9 = {14{1'b0}};
endmodule
